// Logisim project l64.circ as structural Verilog: 11 circuits, main circuit main
module main (
);

  wire and_1_out, and_2_out, comparator_1_eq, comparator_2_eq, MasterClock, MemEnable, MemWrite, not_1_out,
       Reset;
  wire [1:0] Size;
  wire [6:0] bit_extender_1_out;
  wire [7:0] rom_1_p2, rom_1_p3, rom_1_p4, rom_1_p5, rom_1_p6, rom_1_p7, rom_1_p8, rom_1_p9;
  wire [63:0] Address, cpu_1_writedata, Data, memorytruncater_1_data, register_1_q;

  // ROM #(.addrWidth(16), .line("octo"), .misaligned("true")) rom_1: pin names not known; wires that end beside it: Address[15:0], rom_1_p2, rom_1_p3, rom_1_p4, rom_1_p5, rom_1_p6, rom_1_p7, rom_1_p8, rom_1_p9
  Clock u_MasterClock (.out(MasterClock));
  Button u_Reset (.out(Reset));
  CPU cpu_1 (
    .ReadData(Data), .Clock(MasterClock), .Reset(Reset), .MemoryEnable(MemEnable), .WriteEnable(MemWrite),
    .WriteData(cpu_1_writedata), .Address(Address), .Size(Size));
  assign Data = MemWrite ? cpu_1_writedata : 64'bz;  // Controlled_Buffer controlled_buffer_1
  MemoryTruncater memorytruncater_1 (
    .Size(Size), .Byte0(rom_1_p2), .Byte1(rom_1_p3), .Byte2(rom_1_p4), .Byte3(rom_1_p5), .Byte4(rom_1_p6),
    .Byte5(rom_1_p7), .Byte6(rom_1_p8), .Byte7(rom_1_p9), .Data(memorytruncater_1_data));
  Comparator #(.mode("unsigned"), .width(48)) comparator_1 (
    .a(Address[63:16]), .b({48{1'b0}}), .eq(comparator_1_eq));  // open: gt, lt
  and and_1 (and_1_out, comparator_1_eq, MemEnable, ~MemWrite);  // AND_Gate
  assign Data = and_1_out ? memorytruncater_1_data : 64'bz;  // Controlled_Buffer controlled_buffer_2
  Bit_Extender #(.in_width(64), .out_width(7), .\type ("zero")) bit_extender_1 (.in(Data), .out(bit_extender_1_out));
  TTY tty_1 (.data(bit_extender_1_out), .clk(MasterClock), .we(and_2_out), .clr(Reset));
  Comparator #(.mode("unsigned"), .width(48)) comparator_2 (
    .a(Address[63:16]), .b({48{1'b0}}), .eq(comparator_2_eq));  // open: gt, lt
  and and_2 (and_2_out, MemEnable, MemWrite, not_1_out);
  not not_1 (not_1_out, comparator_2_eq);
  Register #(.width(64)) register_1 (.D(Data), .en(and_2_out), .clk(MasterClock), .Q(register_1_q), .clr(Reset));
  // Probe on register_1_q
  Counter #(.max('hf), .width(4)) counter_1 (
    .clr(Reset), .load(and_2_out), .up(1'b1), .count(1'b1), .clk(MasterClock), .D(4'b0000));  // open: carry, Q

  // Notes on the sheet:
  //   contents of rom_1 (hex, n*v repeats v):
  //   6 e0 df 37 10 0 0 0 7 e0 1 a 4*0 7 40 0 a 4*0 4a 0 0 32 d 0 0 0 b fe 1 34 48 0 0 0 43 60 0 0 50 0 0
  //   0 2 0 6 0 0 0 1 0 46 40 0 a 1 0 0 0 7 e0 1 a 18 0 0 0 c4 e1 1 a 4*0 48 65 6c 6c 6f 20 57 6f 72 6c 64
  //   21 a
endmodule

module RegFile (
  input  Write0Enable,
  input  Write1Enable,
  input  [3:0] Write0Reg,
  input  [3:0] Write1Reg,
  input  [63:0] Write0Data,
  input  [63:0] Write1Data,
  input  [3:0] Read0Reg,
  input  [3:0] Read1Reg,
  input  [3:0] Read2Reg,
  input  RIPOverride,
  input  [63:0] RIPData,
  input  Reset,
  input  Clock,
  output [63:0] Read0Out,
  output [63:0] Read1Out,
  output [63:0] Read2Out,
  output [63:0] RIP,
  output CanPretend
);

  wire demultiplexer_1_out1, demultiplexer_1_out2, demultiplexer_1_out3, demultiplexer_1_out4,
       demultiplexer_1_out5, demultiplexer_1_out6, demultiplexer_1_out7, demultiplexer_1_out8,
       demultiplexer_1_out9, demultiplexer_1_out10, demultiplexer_1_out11, demultiplexer_1_out12,
       demultiplexer_1_out13, demultiplexer_1_out14, demultiplexer_1_out15, demultiplexer_2_out1,
       demultiplexer_2_out2, demultiplexer_2_out3, demultiplexer_2_out4, demultiplexer_2_out5,
       demultiplexer_2_out6, demultiplexer_2_out7, demultiplexer_2_out8, demultiplexer_2_out9,
       demultiplexer_2_out10, demultiplexer_2_out11, demultiplexer_2_out12, demultiplexer_2_out13,
       demultiplexer_2_out14, demultiplexer_2_out15, or_1_out, or_2_out, or_3_out, or_4_out, or_5_out,
       or_6_out, or_7_out, or_8_out, or_9_out, or_10_out, or_11_out, or_12_out, or_13_out, or_14_out,
       or_15_out;
  wire [63:0] multiplexer_1_out, multiplexer_2_out, multiplexer_3_out, multiplexer_4_out, multiplexer_5_out,
       multiplexer_6_out, multiplexer_7_out, multiplexer_8_out, multiplexer_9_out, multiplexer_10_out,
       multiplexer_11_out, multiplexer_12_out, multiplexer_13_out, multiplexer_14_out, multiplexer_15_out,
       multiplexer_16_out, register_1_q, register_2_q, register_3_q, register_4_q, register_5_q,
       register_6_q, register_7_q, register_8_q, register_9_q, register_10_q, register_11_q, register_12_q,
       register_13_q, register_14_q;

  Demultiplexer #(.select(4)) demultiplexer_1 (
    .out1(demultiplexer_1_out1), .out2(demultiplexer_1_out2), .out3(demultiplexer_1_out3),
    .out4(demultiplexer_1_out4), .out5(demultiplexer_1_out5), .out6(demultiplexer_1_out6),
    .out7(demultiplexer_1_out7), .out8(demultiplexer_1_out8), .out9(demultiplexer_1_out9),
    .out10(demultiplexer_1_out10), .out11(demultiplexer_1_out11), .out12(demultiplexer_1_out12),
    .out13(demultiplexer_1_out13), .out14(demultiplexer_1_out14), .out15(demultiplexer_1_out15),
    .in(Write1Enable), .sel(Write1Reg));  // open: out0
  Demultiplexer #(.select(4)) demultiplexer_2 (
    .out1(demultiplexer_2_out1), .out2(demultiplexer_2_out2), .out3(demultiplexer_2_out3),
    .out4(demultiplexer_2_out4), .out5(demultiplexer_2_out5), .out6(demultiplexer_2_out6),
    .out7(demultiplexer_2_out7), .out8(demultiplexer_2_out8), .out9(demultiplexer_2_out9),
    .out10(demultiplexer_2_out10), .out11(demultiplexer_2_out11), .out12(demultiplexer_2_out12),
    .out13(demultiplexer_2_out13), .out14(demultiplexer_2_out14), .out15(demultiplexer_2_out15),
    .in(Write0Enable), .sel(Write0Reg));  // open: out0
  nor nor_1 (CanPretend, demultiplexer_1_out15, demultiplexer_2_out15);
  Register #(.width(64)) register_1 (.D(multiplexer_1_out), .en(or_1_out), .clk(Clock), .Q(register_1_q), .clr(Reset));
  Multiplexer #(.disabled("Z"), .width(64)) multiplexer_1 (
    .in0(Write0Data), .in1(Write1Data), .out(multiplexer_1_out), .sel(demultiplexer_1_out1));
  or or_1 (or_1_out, demultiplexer_2_out1, demultiplexer_1_out1);
  Register #(.width(64)) register_2 (.D(multiplexer_2_out), .en(or_2_out), .clk(Clock), .Q(register_2_q), .clr(Reset));
  Multiplexer #(.disabled("Z"), .width(64)) multiplexer_2 (
    .in0(Write0Data), .in1(Write1Data), .out(multiplexer_2_out), .sel(demultiplexer_1_out2));
  or or_2 (or_2_out, demultiplexer_2_out2, demultiplexer_1_out2);
  Register #(.width(64)) register_3 (.D(multiplexer_3_out), .en(or_3_out), .clk(Clock), .Q(register_3_q), .clr(Reset));
  Multiplexer #(.disabled("Z"), .width(64)) multiplexer_3 (
    .in0(Write0Data), .in1(Write1Data), .out(multiplexer_3_out), .sel(demultiplexer_1_out3));
  or or_3 (or_3_out, demultiplexer_2_out3, demultiplexer_1_out3);
  Register #(.width(64)) register_4 (.D(multiplexer_4_out), .en(or_4_out), .clk(Clock), .Q(register_4_q), .clr(Reset));
  Multiplexer #(.disabled("Z"), .width(64)) multiplexer_4 (
    .in0(Write0Data), .in1(Write1Data), .out(multiplexer_4_out), .sel(demultiplexer_1_out4));
  or or_4 (or_4_out, demultiplexer_2_out4, demultiplexer_1_out4);
  Register #(.width(64)) register_5 (.D(multiplexer_5_out), .en(or_5_out), .clk(Clock), .Q(register_5_q), .clr(Reset));
  Multiplexer #(.disabled("Z"), .width(64)) multiplexer_5 (
    .in0(Write0Data), .in1(Write1Data), .out(multiplexer_5_out), .sel(demultiplexer_1_out5));
  or or_5 (or_5_out, demultiplexer_2_out5, demultiplexer_1_out5);
  Register #(.width(64)) register_6 (.D(multiplexer_6_out), .en(or_6_out), .clk(Clock), .Q(register_6_q), .clr(Reset));
  Multiplexer #(.disabled("Z"), .width(64)) multiplexer_6 (
    .in0(Write0Data), .in1(Write1Data), .out(multiplexer_6_out), .sel(demultiplexer_1_out6));
  or or_6 (or_6_out, demultiplexer_2_out6, demultiplexer_1_out6);
  Register #(.width(64)) register_7 (.D(multiplexer_7_out), .en(or_7_out), .clk(Clock), .Q(register_7_q), .clr(Reset));
  Multiplexer #(.disabled("Z"), .width(64)) multiplexer_7 (
    .in0(Write0Data), .in1(Write1Data), .out(multiplexer_7_out), .sel(demultiplexer_1_out7));
  or or_7 (or_7_out, demultiplexer_2_out7, demultiplexer_1_out7);
  Register #(.width(64)) register_8 (.D(multiplexer_8_out), .en(or_8_out), .clk(Clock), .Q(register_8_q), .clr(Reset));
  Multiplexer #(.disabled("Z"), .width(64)) multiplexer_8 (
    .in0(Write0Data), .in1(Write1Data), .out(multiplexer_8_out), .sel(demultiplexer_1_out8));
  or or_8 (or_8_out, demultiplexer_2_out8, demultiplexer_1_out8);
  Register #(.width(64)) register_9 (.D(multiplexer_9_out), .en(or_9_out), .clk(Clock), .Q(register_9_q), .clr(Reset));
  Multiplexer #(.disabled("Z"), .width(64)) multiplexer_9 (
    .in0(Write0Data), .in1(Write1Data), .out(multiplexer_9_out), .sel(demultiplexer_1_out9));
  or or_9 (or_9_out, demultiplexer_2_out9, demultiplexer_1_out9);
  Register #(.width(64)) register_10 (
    .D(multiplexer_10_out), .en(or_10_out), .clk(Clock), .Q(register_10_q), .clr(Reset));
  Multiplexer #(.disabled("Z"), .width(64)) multiplexer_10 (
    .in0(Write0Data), .in1(Write1Data), .out(multiplexer_10_out), .sel(demultiplexer_1_out10));
  or or_10 (or_10_out, demultiplexer_2_out10, demultiplexer_1_out10);
  Register #(.width(64)) register_11 (
    .D(multiplexer_11_out), .en(or_11_out), .clk(Clock), .Q(register_11_q), .clr(Reset));
  Multiplexer #(.disabled("Z"), .width(64)) multiplexer_11 (
    .in0(Write0Data), .in1(Write1Data), .out(multiplexer_11_out), .sel(demultiplexer_1_out11));
  or or_11 (or_11_out, demultiplexer_2_out11, demultiplexer_1_out11);
  Register #(.width(64)) register_12 (
    .D(multiplexer_12_out), .en(or_12_out), .clk(Clock), .Q(register_12_q), .clr(Reset));
  Multiplexer #(.disabled("Z"), .width(64)) multiplexer_12 (
    .in0(Write0Data), .in1(Write1Data), .out(multiplexer_12_out), .sel(demultiplexer_1_out12));
  or or_12 (or_12_out, demultiplexer_2_out12, demultiplexer_1_out12);
  Register #(.width(64)) register_13 (
    .D(multiplexer_13_out), .en(or_13_out), .clk(Clock), .Q(register_13_q), .clr(Reset));
  Multiplexer #(.disabled("Z"), .width(64)) multiplexer_13 (
    .in0(Write0Data), .in1(Write1Data), .out(multiplexer_13_out), .sel(demultiplexer_1_out13));
  or or_13 (or_13_out, demultiplexer_2_out13, demultiplexer_1_out13);
  Register #(.width(64)) register_14 (
    .D(multiplexer_14_out), .en(or_14_out), .clk(Clock), .Q(register_14_q), .clr(Reset));
  Multiplexer #(.disabled("Z"), .width(64)) multiplexer_14 (
    .in0(Write0Data), .in1(Write1Data), .out(multiplexer_14_out), .sel(demultiplexer_1_out14));
  or or_14 (or_14_out, demultiplexer_2_out14, demultiplexer_1_out14);
  Multiplexer #(.disabled("Z"), .width(64)) multiplexer_15 (
    .in0(Write0Data), .in1(Write1Data), .out(multiplexer_15_out), .sel(demultiplexer_1_out15));
  Register #(.width(64)) register_15 (.D(multiplexer_16_out), .en(or_15_out), .clk(Clock), .Q(RIP), .clr(Reset));
  Multiplexer #(.disabled("Z"), .width(64)) multiplexer_16 (
    .in0(multiplexer_15_out), .in1(RIPData), .out(multiplexer_16_out), .sel(RIPOverride));
  or or_15 (or_15_out, demultiplexer_2_out15, RIPOverride, demultiplexer_1_out15);
  Multiplexer #(.disabled("Z"), .select(4), .width(64)) multiplexer_17 (
    .in0({64{1'b0}}), .in1(register_1_q), .in2(register_2_q), .in3(register_3_q), .in4(register_4_q),
    .in5(register_5_q), .in6(register_6_q), .in7(register_7_q), .in8(register_8_q), .in9(register_9_q),
    .in10(register_10_q), .in11(register_11_q), .in12(register_12_q), .in13(register_13_q),
    .in14(register_14_q), .in15(RIP), .out(Read0Out), .sel(Read0Reg));
  Multiplexer #(.disabled("Z"), .select(4), .width(64)) multiplexer_18 (
    .in0({64{1'b0}}), .in1(register_1_q), .in2(register_2_q), .in3(register_3_q), .in4(register_4_q),
    .in5(register_5_q), .in6(register_6_q), .in7(register_7_q), .in8(register_8_q), .in9(register_9_q),
    .in10(register_10_q), .in11(register_11_q), .in12(register_12_q), .in13(register_13_q),
    .in14(register_14_q), .in15(RIP), .out(Read1Out), .sel(Read1Reg));
  Multiplexer #(.disabled("Z"), .select(4), .width(64)) multiplexer_19 (
    .in0({64{1'b0}}), .in1(register_1_q), .in2(register_2_q), .in3(register_3_q), .in4(register_4_q),
    .in5(register_5_q), .in6(register_6_q), .in7(register_7_q), .in8(register_8_q), .in9(register_9_q),
    .in10(register_10_q), .in11(register_11_q), .in12(register_12_q), .in13(register_13_q),
    .in14(register_14_q), .in15(RIP), .out(Read2Out), .sel(Read2Reg));
endmodule

module ALU (
  input  [5:0] Op,
  input  [63:0] A,
  input  [63:0] B,
  input  [63:0] C,
  output [63:0] O,
  output [63:0] I
);

  wire adder_1_cout, comparator_1_eq, decoder_1_out0, decoder_1_out1, decoder_1_out2, decoder_1_out3,
       decoder_1_out4, decoder_1_out5, decoder_1_out6, decoder_1_out7, decoder_1_out8, decoder_1_out13,
       decoder_1_out14, decoder_1_out15, decoder_1_out16, decoder_1_out17, decoder_1_out18, decoder_1_out19,
       decoder_1_out20, decoder_1_out21, decoder_1_out22, decoder_1_out23, decoder_1_out24, decoder_1_out25,
       decoder_1_out26, decoder_1_out27, decoder_1_out28, decoder_1_out29, not_1_out, not_2_out, or_2_out,
       or_3_out, or_4_out, subtractor_1_bout;
  wire [3:0] bit_extender_1_out, decoder_1_out9;
  wire [7:0] bit_extender_7_out;
  wire [15:0] bit_extender_6_out;
  wire [31:0] bit_extender_4_out;
  wire [63:0] adder_1_out, adder_2_out, and_1_out, bit_extender_2_out, bit_extender_3_out,
       bit_extender_5_out, bit_extender_8_out, bit_extender_9_out, multiplier_1_cout, multiplier_1_out,
       multiplier_2_cout, multiplier_2_out, negator_1_out, or_1_out, subtractor_1_out, xor_1_out;

  not not_1 (not_1_out, Op[5]);
  Bit_Extender #(.in_width(6), .out_width(4), .\type ("zero")) bit_extender_1 (.in(Op), .out(bit_extender_1_out));
  not not_2 (not_2_out, comparator_1_eq);
  Comparator #(.mode("unsigned"), .width(64)) comparator_1 (
    .a(C), .b({64{1'b0}}), .eq(comparator_1_eq));  // open: gt, lt
  assign and_1_out = B & A;  // AND_Gate and_1, 64 bits wide
  assign O = decoder_1_out0 ? and_1_out : 64'bz;  // Controlled_Buffer controlled_buffer_1
  assign or_1_out = B | A;  // OR_Gate or_1, 64 bits wide
  assign O = decoder_1_out1 ? or_1_out : 64'bz;  // Controlled_Buffer controlled_buffer_2
  assign xor_1_out = B ^ A;  // XOR_Gate xor_1, 64 bits wide
  assign O = decoder_1_out2 ? xor_1_out : 64'bz;  // Controlled_Buffer controlled_buffer_3
  assign O = decoder_1_out3 ? ~A : 64'bz;  // Controlled_Inverter controlled_inverter_1
  assign O = decoder_1_out4 ? negator_1_out : 64'bz;  // Controlled_Buffer controlled_buffer_4
  Negator #(.width(64)) negator_1 (.in(A), .out(negator_1_out));
  Adder #(.width(64)) adder_1 (.a(A), .b(B), .out(adder_1_out), .cin(not_2_out), .cout(adder_1_cout));
  assign bit_extender_2_out = {{63{1'b0}}, adder_1_cout};  // Bit_Extender bit_extender_2
  assign I = decoder_1_out5 ? bit_extender_2_out : 64'bz;  // Controlled_Buffer controlled_buffer_5
  assign O = decoder_1_out5 ? adder_1_out : 64'bz;  // Controlled_Buffer controlled_buffer_6
  Subtractor #(.width(64)) subtractor_1 (
    .a(A), .b(B), .out(subtractor_1_out), .bin(not_2_out), .bout(subtractor_1_bout));
  assign bit_extender_3_out = {{63{1'b0}}, subtractor_1_bout};  // Bit_Extender bit_extender_3
  assign I = decoder_1_out6 ? bit_extender_3_out : 64'bz;  // Controlled_Buffer controlled_buffer_7
  assign O = decoder_1_out6 ? subtractor_1_out : 64'bz;  // Controlled_Buffer controlled_buffer_8
  Multiplier #(.width(64)) multiplier_1 (.a(A), .b(B), .out(multiplier_1_out), .cin(C), .cout(multiplier_1_cout));
  assign I = decoder_1_out7 ? multiplier_1_cout : 64'bz;  // Controlled_Buffer controlled_buffer_9
  assign O = decoder_1_out7 ? multiplier_1_out : 64'bz;  // Controlled_Buffer controlled_buffer_10
  Multiplier #(.mode("twosComplement"), .width(64)) multiplier_2 (
    .a(A), .b(B), .out(multiplier_2_out), .cin(C), .cout(multiplier_2_cout));
  assign I = decoder_1_out8 ? multiplier_2_cout : 64'bz;  // Controlled_Buffer controlled_buffer_11
  assign O = decoder_1_out8 ? multiplier_2_out : 64'bz;  // Controlled_Buffer controlled_buffer_12
  Decoder #(.select(5)) decoder_1 (
    .out0(decoder_1_out0), .out1(decoder_1_out1), .out2(decoder_1_out2), .out3(decoder_1_out3),
    .out4(decoder_1_out4), .out5(decoder_1_out5), .out6(decoder_1_out6), .out7(decoder_1_out7),
    .out8(decoder_1_out8), .out9(decoder_1_out9[0]), .out10(decoder_1_out9[1]), .out11(decoder_1_out9[2]),
    .out12(decoder_1_out9[3]), .out13(decoder_1_out13), .out14(decoder_1_out14), .out15(decoder_1_out15),
    .out16(decoder_1_out16), .out17(decoder_1_out17), .out18(decoder_1_out18), .out19(decoder_1_out19),
    .out20(decoder_1_out20), .out21(decoder_1_out21), .out22(decoder_1_out22), .out23(decoder_1_out23),
    .out24(decoder_1_out24), .out25(decoder_1_out25), .out26(decoder_1_out26), .out27(decoder_1_out27),
    .out28(decoder_1_out28), .out29(decoder_1_out29), .sel(Op[4:0]), .en(not_1_out));  // open: out30, out31
  ShiftUnit shiftunit_1 (.Op(decoder_1_out9), .A(A), .B(B), .Result(O));
  or or_2 (or_2_out, decoder_1_out16, decoder_1_out17, decoder_1_out18, decoder_1_out19, decoder_1_out20);
  or or_3 (or_3_out, decoder_1_out21, decoder_1_out22, decoder_1_out23, decoder_1_out24, decoder_1_out25);
  or or_4 (or_4_out, or_2_out, or_3_out);
  Bit_Extender #(.in_width(64), .out_width(32), .\type ("zero")) bit_extender_4 (.in(A), .out(bit_extender_4_out));
  assign bit_extender_5_out = {{32{bit_extender_4_out[31]}}, bit_extender_4_out};  // Bit_Extender bit_extender_5
  Bit_Extender #(.in_width(32), .\type ("zero")) bit_extender_6 (.in(bit_extender_4_out), .out(bit_extender_6_out));
  Bit_Extender #(.in_width(16), .out_width(8), .\type ("zero")) bit_extender_7 (
    .in(bit_extender_6_out), .out(bit_extender_7_out));
  assign bit_extender_8_out = {{48{bit_extender_6_out[15]}}, bit_extender_6_out};  // Bit_Extender bit_extender_8
  assign O = decoder_1_out15 ? bit_extender_5_out : 64'bz;  // Controlled_Buffer controlled_buffer_13
  assign O = decoder_1_out14 ? bit_extender_8_out : 64'bz;  // Controlled_Buffer controlled_buffer_14
  assign bit_extender_9_out = {{56{bit_extender_7_out[7]}}, bit_extender_7_out};  // Bit_Extender bit_extender_9
  assign O = decoder_1_out13 ? bit_extender_9_out : 64'bz;  // Controlled_Buffer controlled_buffer_15
  CompUnit compunit_1 (.Enable(or_4_out), .Op(bit_extender_1_out), .A(A), .B(B), .O(O), .I(I));
  assign I = decoder_1_out26 ? C : 64'bz;  // Controlled_Buffer controlled_buffer_16
  Multiplexer #(.disabled("Z"), .enable("true"), .width(64)) multiplexer_1 (
    .in0(B), .in1(A), .out(O), .sel(not_2_out), .en(decoder_1_out26));
  Adder #(.width(64)) adder_2 (.a(A), .b(B), .out(adder_2_out), .cin(1'b0));  // open: cout
  assign O = decoder_1_out27 ? adder_2_out : 64'bz;  // Controlled_Buffer controlled_buffer_17
  assign I = decoder_1_out27 ? C : 64'bz;  // Controlled_Buffer controlled_buffer_18
  assign O = decoder_1_out28 ? A : 64'bz;  // Controlled_Buffer controlled_buffer_19
  assign I = decoder_1_out28 ? B : 64'bz;  // Controlled_Buffer controlled_buffer_20
  assign O = decoder_1_out29 ? C : 64'bz;  // Controlled_Buffer controlled_buffer_21
  assign I = decoder_1_out29 ? C : 64'bz;  // Controlled_Buffer controlled_buffer_22
endmodule

module CPU (
  input  [63:0] ReadData,
  input  Clock,
  input  Reset,
  output MemoryEnable,
  output WriteEnable,
  output [63:0] WriteData,
  output [63:0] Address,
  output [1:0] Size
);

  wire aludriver_1_writeflags, and_1_out, and_2_out, CanPretend, ConnectAddress, ConnectMemory,
       microcode_1_addressmode, microcode_1_cycledisable, microcode_1_flagsmode, microcode_1_memoryenable,
       microcode_1_memorywrite, microcode_1_pretendloadstate, microcode_1_regwrite0enable,
       microcode_1_regwrite1enable, microcode_1_statereset, not_1_out, State_qn, StateExecute, StateLoad;
  wire [1:0] addressunit_1_size, instructiondecoder_1_loadsize, instructiondecoder_1_storesize,
       microcode_1_immediatemode;
  wire [3:0] Cycle_q;
  wire [4:0] Opcode;
  wire [5:0] ALUOp;
  wire [11:0] instructiondecoder_1_loadscale, instructiondecoder_1_storescale;
  wire [19:0] Registers;
  wire [63:0] addressunit_1_address, alu_1_i, alu_1_o, aludriver_1_a, aludriver_1_b, aludriver_1_c, Flags_q,
       Immediate, InstructionLatch_q, multiplexer_1_out, multiplexer_2_out, NewRIP, RIP, Src0, Src1;

  Microcode microcode_1 (
    .Opcode(Opcode), .Cycle(Cycle_q), .Enable(StateExecute), .RegWrite0Enable(microcode_1_regwrite0enable),
    .RegWrite1Enable(microcode_1_regwrite1enable), .ImmediateMode(microcode_1_immediatemode),
    .FlagsMode(microcode_1_flagsmode), .MemoryEnable(microcode_1_memoryenable),
    .MemoryWrite(microcode_1_memorywrite), .CycleDisable(microcode_1_cycledisable),
    .StateReset(microcode_1_statereset), .AddressMode(microcode_1_addressmode),
    .ConnectMemory(ConnectMemory), .ConnectAddress(ConnectAddress),
    .PretendLoadState(microcode_1_pretendloadstate));
  RegFile regfile_1 (
    .Write0Enable(microcode_1_regwrite0enable), .Write1Enable(microcode_1_regwrite1enable),
    .Write0Reg(Registers[3:0]), .Write1Reg(Registers[7:4]), .Write0Data(multiplexer_1_out),
    .Write1Data(alu_1_i), .Read0Reg(Registers[11:8]), .Read1Reg(Registers[15:12]),
    .Read2Reg(Registers[19:16]), .RIPOverride(StateLoad), .RIPData(NewRIP), .Reset(Reset), .Clock(Clock),
    .Read0Out(Src0), .Read1Out(Src1), .Read2Out(WriteData), .RIP(RIP), .CanPretend(CanPretend));
  and and_1 (and_1_out, microcode_1_statereset, ~and_2_out);  // AND_Gate
  and and_2 (and_2_out, microcode_1_pretendloadstate, CanPretend);
  Counter #(.max('hf), .width(4)) Cycle (
    .clr(1'b0), .load(StateLoad), .up(1'b1), .count(not_1_out), .clk(Clock), .D(4'b0000), .Q(Cycle_q));  // open: carry
  not not_1 (not_1_out, microcode_1_cycledisable);
  S_R_Flip_Flop State (
    .S(StateLoad), .R(and_1_out), .clk(Clock), .Q(StateExecute), .reset(Reset), .Qn(State_qn));  // open: preset
  or or_1 (StateLoad, State_qn, and_2_out);
  Register #(.width(64)) InstructionLatch (
    .D(ReadData), .en(StateLoad), .clk(Clock), .Q(InstructionLatch_q), .clr(Reset));
  Adder #(.width(64)) adder_1 (.a(RIP), .b(64'h8), .out(NewRIP), .cin(1'b0));  // open: cout
  InstructionDecoder instructiondecoder_1 (
    .Instruction(InstructionLatch_q), .OpCode(Opcode), .ALUOp(ALUOp), .Immediate(Immediate),
    .Src0(Registers[11:8]), .Src1(Registers[15:12]), .Dst0(Registers[3:0]), .Src2(Registers[19:16]),
    .Dst1(Registers[7:4]), .StoreScale(instructiondecoder_1_storescale),
    .LoadScale(instructiondecoder_1_loadscale), .StoreSize(instructiondecoder_1_storesize),
    .LoadSize(instructiondecoder_1_loadsize));
  ALUDriver aludriver_1 (
    .Reg0(Src0), .Reg1(Src1), .Reg2(WriteData), .Immediate(Immediate), .Flags(Flags_q),
    .ImmediateMode(microcode_1_immediatemode), .FlagsMode(microcode_1_flagsmode), .A(aludriver_1_a),
    .B(aludriver_1_b), .C(aludriver_1_c), .WriteFlags(aludriver_1_writeflags));
  Register #(.width(64)) Flags (.D(alu_1_i), .en(aludriver_1_writeflags), .clk(Clock), .Q(Flags_q), .clr(Reset));
  ALU alu_1 (.Op(ALUOp), .A(aludriver_1_a), .B(aludriver_1_b), .C(aludriver_1_c), .O(alu_1_o), .I(alu_1_i));
  Multiplexer #(.disabled("Z"), .width(64)) multiplexer_1 (
    .in0(alu_1_o), .in1(multiplexer_2_out), .out(multiplexer_1_out), .sel(ConnectAddress));
  Multiplexer #(.disabled("Z"), .width(64)) multiplexer_2 (
    .in0(Address), .in1(ReadData), .out(multiplexer_2_out), .sel(ConnectMemory));
  Multiplexer #(.width(64)) multiplexer_3 (.in0(addressunit_1_address), .in1(RIP), .out(Address), .sel(StateLoad));
  AddressUnit addressunit_1 (
    .Base(Src0), .Offset(Immediate), .Index(Src1), .StoreScale(instructiondecoder_1_storescale),
    .LoadScale(instructiondecoder_1_loadscale), .StoreSize(instructiondecoder_1_storesize),
    .LoadSize(instructiondecoder_1_loadsize), .Mode(microcode_1_addressmode),
    .Address(addressunit_1_address), .Size(addressunit_1_size));
  or or_2 (MemoryEnable, microcode_1_memoryenable, StateLoad);
  and and_3 (WriteEnable, microcode_1_memorywrite, ~StateLoad);  // AND_Gate
  Multiplexer #(.width(2)) multiplexer_4 (.in0(addressunit_1_size), .in1(2'b11), .out(Size), .sel(StateLoad));

  // Other names for the same wires on the sheet: Src2[63:0] = WriteData
endmodule

module ALUDriver (
  input  [63:0] Reg0,
  input  [63:0] Reg1,
  input  [63:0] Reg2,
  input  [63:0] Immediate,
  input  [63:0] Flags,
  input  [1:0] ImmediateMode,
  input  FlagsMode,
  output [63:0] A,
  output [63:0] B,
  output [63:0] C,
  output WriteFlags
);

  wire decoder_1_out1, decoder_1_out2, decoder_1_out3;
  wire [63:0] multiplexer_1_out;

  Decoder #(.enable("false"), .select(2)) decoder_1 (
    .out1(decoder_1_out1), .out2(decoder_1_out2), .out3(decoder_1_out3), .sel(ImmediateMode));  // open: out0
  Multiplexer #(.width(64)) multiplexer_1 (.in0(Reg2), .in1(Immediate), .out(multiplexer_1_out), .sel(decoder_1_out3));
  Multiplexer #(.width(64)) multiplexer_2 (.in0(Reg0), .in1(Immediate), .out(A), .sel(decoder_1_out1));
  Multiplexer #(.width(64)) multiplexer_3 (.in0(Reg1), .in1(Immediate), .out(B), .sel(decoder_1_out2));
  Multiplexer #(.width(64)) multiplexer_4 (.in0(multiplexer_1_out), .in1(Flags), .out(C), .sel(FlagsMode));

  assign WriteFlags = FlagsMode;
endmodule

module InstructionDecoder (
  input  [63:0] Instruction,
  output [4:0] OpCode,
  output [5:0] ALUOp,
  output [63:0] Immediate,
  output [3:0] Src0,
  output [3:0] Src1,
  output [3:0] Dst0,
  output [3:0] Src2,
  output [3:0] Dst1,
  output [11:0] StoreScale,
  output [11:0] LoadScale,
  output [1:0] StoreSize,
  output [1:0] LoadSize
);

  assign Immediate = {{32{Instruction[63]}}, Instruction[63:32]};  // Bit_Extender bit_extender_1

  assign ALUOp = Instruction[30:25];
  assign Dst0 = Instruction[16:13];
  assign Dst1 = Instruction[24:21];
  assign LoadScale = Instruction[30:19];
  assign LoadSize = Instruction[18:17];
  assign OpCode = Instruction[4:0];
  assign Src0 = Instruction[8:5];
  assign Src1 = Instruction[12:9];
  assign Src2 = Instruction[20:17];
  assign StoreScale = {Instruction[30:21], Instruction[16:15]};
  assign StoreSize = Instruction[14:13];
endmodule

module AddressUnit (
  input  [63:0] Base,
  input  [63:0] Offset,
  input  [63:0] Index,
  input  [11:0] StoreScale,
  input  [11:0] LoadScale,
  input  [1:0] StoreSize,
  input  [1:0] LoadSize,
  input  Mode,
  output [63:0] Address,
  output [1:0] Size
);

  wire [11:0] multiplexer_1_out;
  wire [63:0] adder_1_out, adder_2_out, bit_extender_1_out, multiplier_1_out;

  Adder #(.width(64)) adder_1 (.a(Base), .b(Offset), .out(adder_1_out), .cin(1'b0));  // open: cout
  assign bit_extender_1_out = {{52{1'b0}}, multiplexer_1_out};  // Bit_Extender bit_extender_1
  Multiplexer #(.width(12)) multiplexer_1 (.in0(StoreScale), .in1(LoadScale), .out(multiplexer_1_out), .sel(Mode));
  Multiplexer #(.width(2)) multiplexer_2 (.in0(StoreSize), .in1(LoadSize), .out(Size), .sel(Mode));
  Multiplier #(.width(64)) multiplier_1 (
    .a(Index), .b(adder_2_out), .out(multiplier_1_out), .cin({64{1'b0}}));  // open: cout
  Adder #(.width(64)) adder_2 (.a(bit_extender_1_out), .b({64{1'b0}}), .out(adder_2_out), .cin(1'b1));  // open: cout
  Adder #(.width(64)) adder_3 (.a(adder_1_out), .b(multiplier_1_out), .out(Address), .cin(1'b0));  // open: cout
endmodule

module Microcode (
  input  [4:0] Opcode,
  input  [3:0] Cycle,
  input  Enable,
  output RegWrite0Enable,
  output RegWrite1Enable,
  output [1:0] ImmediateMode,
  output FlagsMode,
  output MemoryEnable,
  output MemoryWrite,
  output CycleDisable,
  output StateReset,
  output AddressMode,
  output ConnectMemory,
  output ConnectAddress,
  output PretendLoadState
);

  wire [12:0] pla_1_out;

  PLA #(.in_width(9), .out_width(13), .\table ("000000000 1000000000000 # NOP\n001110000 1000100000111 # ALU4\n001000000 1000100000011 # ALU1\n000100000 0000101100000 # Store\n001010000 1000100001111 # ALU2\n001100000 1000100001011 # ALU3\n010000000 1000100010011 # ALU5\n010100000 1000100011011 # ALU6\n010110000 1000100010111 # ALU7\n000110000 0111100100001 # Load\n000010000 1101100000001 # Lea")) pla_1 (
    .in({Opcode, Cycle}), .out(pla_1_out));
  and and_1 (RegWrite0Enable, pla_1_out[0], Enable);
  and and_2 (RegWrite1Enable, pla_1_out[1], Enable);
  Multiplexer #(.disabled("Z"), .width(2)) multiplexer_1 (
    .in0(2'b00), .in1(pla_1_out[3:2]), .out(ImmediateMode), .sel(Enable));
  and and_3 (FlagsMode, pla_1_out[4], Enable);
  and and_4 (MemoryEnable, pla_1_out[5], Enable);
  and and_5 (MemoryWrite, pla_1_out[6], Enable);
  and and_6 (CycleDisable, pla_1_out[7], Enable);
  and and_7 (StateReset, pla_1_out[8], Enable);
  and and_8 (AddressMode, pla_1_out[9], Enable);
  and and_9 (ConnectMemory, pla_1_out[10], Enable);
  and and_10 (ConnectAddress, pla_1_out[11], Enable);
  and and_11 (PretendLoadState, pla_1_out[12], Enable);
endmodule

module MemoryTruncater (
  input  [1:0] Size,
  input  [7:0] Byte0,
  input  [7:0] Byte1,
  input  [7:0] Byte2,
  input  [7:0] Byte3,
  input  [7:0] Byte4,
  input  [7:0] Byte5,
  input  [7:0] Byte6,
  input  [7:0] Byte7,
  output [63:0] Data
);

  wire and_1_out, or_1_out;

  Multiplexer #(.disabled("Z"), .width(8)) multiplexer_1 (
    .in0({8{1'b0}}), .in1(Byte1), .out(Data[15:8]), .sel(or_1_out));
  Multiplexer #(.disabled("Z"), .width(16)) multiplexer_2 (
    .in0({16{1'b0}}), .in1({Byte3, Byte2}), .out(Data[31:16]), .sel(Size[1]));
  Multiplexer #(.disabled("Z"), .width(32)) multiplexer_3 (
    .in0({32{1'b0}}), .in1({Byte7, Byte6, Byte5, Byte4}), .out(Data[63:32]), .sel(and_1_out));
  or or_1 (or_1_out, Size[0], Size[1]);
  and and_1 (and_1_out, Size[0], Size[1]);

  assign Data[7:0] = Byte0;
endmodule

module ShiftUnit (
  input  [3:0] Op,
  input  [63:0] A,
  input  [63:0] B,
  output [63:0] Result
);

  wire comparator_1_eq, not_1_out;
  wire [63:0] and_1_out, bit_extender_1_out, or_1_out, shifter_1_out, shifter_2_out, shifter_3_out,
       shifter_4_out;

  Comparator #(.mode("unsigned"), .width(58)) comparator_1 (
    .a(B[63:6]), .b({58{1'b0}}), .eq(comparator_1_eq));  // open: gt, lt
  assign bit_extender_1_out = {{63{B[63]}}, B[63]};  // Bit_Extender bit_extender_1
  not not_1 (not_1_out, comparator_1_eq);
  assign and_1_out = 64'hffffffff & B;  // AND_Gate and_1, 64 bits wide
  Shifter #(.width(64)) shifter_1 (.in(A), .\dist (B[5:0]), .out(shifter_1_out));
  Shifter #(.width(64)) shifter_2 (.in(A), .\dist (6'b100000), .out(shifter_2_out));
  Shifter #(.shift("lr"), .width(64)) shifter_3 (.in(A), .\dist (B[5:0]), .out(shifter_3_out));
  Shifter #(.shift("ar"), .width(64)) shifter_4 (.in(A), .\dist (B[5:0]), .out(shifter_4_out));
  Multiplexer #(.disabled("Z"), .enable("true"), .width(64)) multiplexer_1 (
    .in0(shifter_1_out), .in1({64{1'b0}}), .out(Result), .sel(not_1_out), .en(Op[0]));
  assign or_1_out = shifter_2_out | and_1_out;  // OR_Gate or_1, 64 bits wide
  assign Result = Op[3] ? or_1_out : 64'bz;  // Controlled_Buffer controlled_buffer_1
  Multiplexer #(.disabled("Z"), .enable("true"), .width(64)) multiplexer_2 (
    .in0(shifter_3_out), .in1({64{1'b0}}), .out(Result), .sel(not_1_out), .en(Op[1]));
  Multiplexer #(.disabled("Z"), .enable("true"), .width(64)) multiplexer_3 (
    .in0(shifter_4_out), .in1(bit_extender_1_out), .out(Result), .sel(not_1_out), .en(Op[2]));
endmodule

module CompUnit (
  input  Enable,
  input  [3:0] Op,
  input  [63:0] A,
  input  [63:0] B,
  output [63:0] O,
  output [63:0] I
);

  wire comparator_1_eq, comparator_1_gt, comparator_1_lt, comparator_2_gt, comparator_2_lt,
       multiplexer_1_out, not_1_out, not_2_out, not_3_out, not_4_out, not_5_out;
  wire [63:0] bit_extender_1_out;

  Comparator #(.mode("unsigned"), .width(64)) comparator_1 (
    .a(A), .b(B), .gt(comparator_1_gt), .eq(comparator_1_eq), .lt(comparator_1_lt));
  Comparator #(.width(64)) comparator_2 (.a(A), .b(B), .gt(comparator_2_gt), .lt(comparator_2_lt));  // open: eq
  not not_1 (not_1_out, comparator_1_eq);
  not not_2 (not_2_out, comparator_1_gt);
  not not_3 (not_3_out, comparator_1_lt);
  not not_4 (not_4_out, comparator_2_gt);
  Multiplexer #(.disabled("Z"), .select(4)) multiplexer_1 (
    .in0(comparator_1_eq), .in1(not_1_out), .in2(comparator_1_gt), .in3(not_2_out), .in4(comparator_1_lt),
    .in5(not_3_out), .in6(comparator_2_gt), .in7(not_4_out), .in8(comparator_2_lt), .in9(not_5_out),
    .out(multiplexer_1_out), .sel(Op));  // open: in10, in11, in12, in13, in14, in15
  not not_5 (not_5_out, comparator_2_lt);
  assign bit_extender_1_out = {{63{1'b0}}, multiplexer_1_out};  // Bit_Extender bit_extender_1
  assign I = Enable ? bit_extender_1_out : 64'bz;  // Controlled_Buffer controlled_buffer_1

  assign O = I;
endmodule
